# Fritzing sketch schéma cablage (saved by Fritzing 0.9.3b)

parts:
  Composant1 = Arduino Mega 2560 (Rev3)
  Composant2 = Arduino Motor Shield (Rev3)
  M1 = DC Motor
  Adafruit_HUZZAH_ESP8266_Breakout1 = Adafruit HUZZAH ESP8266 Breakout [part_number=2471]
  M2 = DC Motor

nets:
  N1: Composant1.D19/RX1, Adafruit_HUZZAH_ESP8266_Breakout1.#15
  N2: Composant1.D18/TX1, Adafruit_HUZZAH_ESP8266_Breakout1.#13
  N3: Composant1.IOREF, Composant2.IOREF
  N4: Composant1.3V3, Adafruit_HUZZAH_ESP8266_Breakout1.3V
  5V: Composant1.5V, Composant2.5V
  GND: Composant1.GND, Composant2.GND, Adafruit_HUZZAH_ESP8266_Breakout1.GND
  VIN: Composant1.VIN, Composant2.VIN
  N5: Composant1.D37, Composant2.D11_PWM/B
  N6: Composant1.D39, Composant2.D13/DirB
  N7: Composant1.D45, Composant2.D3_PWM/A
  N8: Composant1.D47, Composant2.D12/DirA
  N9: Composant2.B-, M2.pin_2
  N10: Composant2.B+, M2.pin_1
  N11: Composant2.A-, M1.pin_2
  N12: Composant2.A+, M1.pin_1
